# Fritzing sketch skrtch (saved by Fritzing 0.8.7b)
breadboards: 1

parts:
  WeMos_D1_R1 = WeMos D1 R2
  DHT1 = Humidity and Temperature Sensor DHT11
  Part1 = 12 NeoPixel Ring [part_number=1643]

nets:
  N1: WeMos_D1_R1.D0/RX, Part1.IN
  N2: WeMos_D1_R1.D1/TX, DHT1.Data-signal
  5V: WeMos_D1_R1.5V, DHT1.Vcc, Part1.VDD
  N3: DHT1.GND_1, Part1.GND

custom parts:
  WeMos D1 R2: The D1 R2 is a mini wifi board based on the ESP-8266EX.
  Humidity and Temperature Sensor DHT11: Digital relative humidity & temperature sensor DHT11
  12 NeoPixel Ring: 12 ultra bright smart LED NeoPixels are arranged in a circle with 1.5" (37mm) outer diameter. The rings are 'chainable' - connect the output pin of one to the input pin of another. Use only one microcontroller pin to control as many as you can chain together! Each LED is addressable as the driver chip is inside the LED. Each one has ~18mA constant current drive so the color will be very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
